# Fritzing sketch dub_siren (saved by Fritzing 1.0.1rc)
breadboards: 2

parts:
  SOM1 = Daisy Seed [chip_label=IC package="DIP (Dual Inline) [THT]"]
  R1 = Rotary Potentiometer (Small) [maximum_resistance=100kΩ knob_status=50% package=THT]
  S1 = Pushbutton [package="[THT]"]
  LED1 = LED - 5mm [color="Red (633nm)" current=0.030 package="5 mm [THT]"]
  R2 = Resistor [tolerance=±5% power=0.25 resistance=220 package=THT]
  SPKR1 = Loudspeaker
  R3 = Rotary Potentiometer (Small) [maximum_resistance=100kΩ knob_status=50% package=THT]
  R4 = Rotary Potentiometer (Small) [maximum_resistance=100kΩ knob_status=50% package=THT]
  R5 = Rotary Potentiometer (Small) [maximum_resistance=100kΩ knob_status=50% package=THT]
  R6 = Rotary Potentiometer (Small) [maximum_resistance=100kΩ knob_status=50% package=THT]
  R7 = Rotary Potentiometer (Small) [maximum_resistance=100kΩ knob_status=50% package=THT]
  S2 = Pushbutton [package="[THT]"]
  S3 = Pushbutton [package="[THT]"]
  S4 = Pushbutton [package="[THT]"]
  S5 = Pushbutton [package="[THT]"]
  S6 = Pushbutton [package="[THT]"]
  LED2 = LED - 5mm [color="Red (633nm)" current=0.030 package="5 mm [THT]"]
  LED3 = LED - 5mm [color="Red (633nm)" current=0.030 package="5 mm [THT]"]
  R8 = Resistor [tolerance=±5% power=0.25 resistance=220 package=THT]
  R9 = Resistor [tolerance=±5% power=0.25 resistance=220 package=THT]

nets:
  N1: SOM1.pin_18, SPKR1.pin2
  N2: SOM1.pin_20, SOM1.pin_40, SPKR1.pin1
  N3: SOM1.pin_21, R1.leg2, R3.leg2, R4.leg2, R5.leg2, R6.leg2, R7.leg2
  N4: SOM1.pin_22, R7.wiper
  N5: SOM1.pin_23, R6.wiper
  N6: SOM1.pin_24, R5.wiper
  N7: SOM1.pin_25, R4.wiper
  N8: SOM1.pin_26, R3.wiper
  N9: SOM1.pin_27, R1.wiper
  N10: SOM1.pin_28, S1.Pin_3, S1.Pin_4
  N11: SOM1.pin_29, S2.Pin_3, S2.Pin_4
  N12: SOM1.pin_30, S3.Pin_3, S3.Pin_4
  N13: SOM1.pin_31, S4.Pin_3, S4.Pin_4
  N14: SOM1.pin_32, S5.Pin_3, S5.Pin_4
  N15: SOM1.pin_33, S6.Pin_3, S6.Pin_4
  N16: SOM1.pin_34, LED1.anode
  N17: SOM1.pin_35, LED2.anode
  N18: SOM1.pin_36, LED3.anode
  N19: R1.leg1, S1.Pin_1, S1.Pin_2, R2.Pin_0, R3.leg1, R4.leg1, R5.leg1, R6.leg1, R7.leg1, S2.Pin_1, S2.Pin_2, S3.Pin_1, S3.Pin_2, S4.Pin_1, S4.Pin_2, S5.Pin_1, S5.Pin_2, S6.Pin_1, S6.Pin_2, R8.Pin_0, R9.Pin_0
  N20: LED1.cathode, R2.Pin_1
  N21: LED2.cathode, R8.Pin_1
  N22: LED3.cathode, R9.Pin_1

custom parts:
  Daisy Seed: Daisy is an embedded platform for music. It features everything you need for creating high fidelity audio hardware devices. Just plug in a USB cable and start making sound! No soldering required.
